# Fritzing sketch nano80 (saved by Fritzing 0.9.3b)
breadboards: 1

parts:
  LCD1 = LCD screen
  R1 = Trimmer Potentiometer [maximum_resistance=10kΩ package=THT]
  S7 = Toggle Switch [package=THT]
  LED2 = LED - 5mm [color="Red (633nm)" package="5 mm [THT]"]
  LED1 = LED - 3mm [color="Green (560nm)" package="3 mm [THT]"]
  R2 = Resistor [tolerance=±5% resistance=560 package=THT]
  R3 = Resistor [tolerance=±5% resistance=560 package=THT]
  IC1 = IC, DIP package, 18 pins [chip_label=IC]
  IC2 = IC, DIP package, 18 pins [chip_label=IC]
  LED3 = LED - 5mm [color="Red (633nm)" package="5 mm [THT]"]
  LED4 = LED - 5mm [color="Red (633nm)" package="5 mm [THT]"]
  LED5 = LED - 5mm [color="Red (633nm)" package="5 mm [THT]"]
  LED6 = LED - 5mm [color="Red (633nm)" package="5 mm [THT]"]
  LED7 = LED - 5mm [color="Red (633nm)" package="5 mm [THT]"]
  LED8 = LED - 5mm [color="Red (633nm)" package="5 mm [THT]"]
  LED9 = LED - 5mm [color="Red (633nm)" package="5 mm [THT]"]
  LED10 = LED - 5mm [color="Red (633nm)" package="5 mm [THT]"]
  R4 = Resistor [tolerance=±5% resistance=47 package=THT]
  R5 = Resistor [tolerance=±5% resistance=47 package=THT]
  R6 = Resistor [tolerance=±5% resistance=220 package=THT]
  R7 = Resistor [tolerance=±5% resistance=47 package=THT]
  R8 = Resistor [tolerance=±5% resistance=220 package=THT]
  R9 = Resistor [tolerance=±5% resistance=47 package=THT]
  R10 = Resistor [tolerance=±5% resistance=470 package=THT]
  R11 = Resistor [tolerance=±5% resistance=470 package=THT]
  S8 = Pushbutton [package=THT]
  S9 = Pushbutton [package=THT]
  S10 = Pushbutton [package=THT]
  S11 = Pushbutton [package=THT]
  S12 = Pushbutton [package=THT]
  S13 = Pushbutton [package=THT]
  S14 = Pushbutton [package=THT]
  S15 = Pushbutton [package=THT]
  S16 = Pushbutton [package=THT]
  S17 = Pushbutton [package=THT]
  S18 = Pushbutton [package=THT]
  S19 = Pushbutton [package=THT]
  S20 = Pushbutton [package=THT]
  S21 = Pushbutton [package=THT]
  Part1 = Arduino Nano (Rev3.0)
  IC3 = IC, DIP package, 8 pins [chip_label=IC]

nets:
  GND: LCD1.VSS, LCD1.R/W, LCD1.LED-, R1.leg1, S7.L2, R2.Pin_1, R3.Pin_1, IC1.pin3, IC1.pin4, IC1.pin5, IC1.pin9, IC2.pin4, IC2.pin5, IC2.pin9, R4.Pin_1, R5.Pin_1, R6.Pin_1, R7.Pin_1, R8.Pin_1, R9.Pin_1, R10.Pin_1, R11.Pin_1, S8.leg1, S9.leg1, S10.leg1, S11.leg1, S12.leg1, S13.leg1, S14.leg1, S15.leg1, S16.leg1, S18.leg1, S20.leg1, S21.leg1, IC3.pin4
  VDD: LCD1.VDD, Part1.5V
  N1: LCD1.V0, R1.wiper
  N2: LCD1.RS, Part1.D8
  N3: LCD1.E, Part1.D9
  N4: LCD1.DB4, Part1.D4
  N5: LCD1.DB5, Part1.D5
  N6: LCD1.DB6, Part1.D6
  N7: LCD1.DB7, Part1.D7
  5V: LCD1.LED+, R1.leg2, IC1.pin6, IC1.pin18, IC2.pin3, IC2.pin6, IC2.pin18, IC3.pin8
  N8: S7.COM, Part1.D11/MOSI
  N9: LED2.cathode, R2.Pin_0
  N10: LED2.anode, Part1.D10
  N11: LED1.cathode, R3.Pin_0
  N12: LED1.anode, Part1.D13/SCK
  N13: IC1.pin1, IC2.pin1, Part1.A5, IC3.pin7
  N14: IC1.pin2, IC2.pin2, Part1.A4, IC3.pin6
  N15: IC1.pin10, LED10.anode
  N16: IC1.pin11, LED9.anode
  N17: IC1.pin12, LED8.anode
  N18: IC1.pin13, LED7.anode
  N19: IC1.pin14, LED6.anode
  N20: IC1.pin15, LED5.anode
  N21: IC1.pin16, LED4.anode
  N22: IC1.pin17, LED3.anode
  N23: IC2.pin10, S21.leg0
  N24: IC2.pin11, S20.leg0
  N25: IC2.pin12, S19.leg0
  N26: IC2.pin13, S18.leg0
  N27: IC2.pin14, S17.leg0
  N28: IC2.pin15, S16.leg0
  N29: IC2.pin16, S15.leg0
  N30: IC2.pin17, S14.leg0
  N31: LED3.cathode, R4.Pin_0
  N32: LED4.cathode, R5.Pin_0
  N33: LED5.cathode, R6.Pin_0
  N34: LED6.cathode, R7.Pin_0
  N35: LED7.cathode, R8.Pin_0
  N36: LED8.cathode, R9.Pin_0
  N37: LED9.cathode, R10.Pin_0
  N38: LED10.cathode, R11.Pin_0
  N39: S8.leg0, Part1.D12/MISO
  N40: S9.leg0, Part1.D2
  N41: S10.leg0, Part1.D3
  N42: S11.leg0, Part1.A0
  N43: S12.leg0, Part1.A1
  N44: S13.leg0, Part1.A2

notes:
  Load Addr Low
  Load Data
  STEP +
  Load Addr Hi
  8080 Reset
  STEP -
  Contrast
  Halt/Run
  Run
  Halt
  All 470 ohms
  White LED's
  MCP23008
  Push Button (Momentary)
  Toggle Switches
  MSB
  LSB
  Address 0x20 (output)
  Address 0x24 (input)
  1x8 LCD Display
  Regulated +5 VDC
  Toggle Switch
  12c clk
  i2c Data
  FRAM breakout
